# Fritzing sketch Stairways Basic (saved by Fritzing 0.9.3b)
breadboards: 1

parts:
  Part1 = Adafruit Trinket M0 [part_number="Adafruit #3500"]
  PIR1 = PIR sensor
  PIR2 = PIR sensor
  Part2 = NeoPixel Stick [part_number=1426]
  U1 = SWITCH_SPDT [package=kps-1290]
  R1 = PHOTOCELL [package=photocell]
  R2 = Resistor [tolerance=±5% resistance=220 package="2512 [SMD]"]

nets:
  GND: Part1.GND, PIR1.GND, PIR2.GND, Part2.GND, U1.P, R2.Pin_0
  N1: Part1.D4_A2_PA06_TXD_MOSI, R1.P$1, R2.Pin_1
  N2: Part1.D3_A3_PA07_RXD_SCK, PIR2.SIG
  N3: Part1.D2_A1_PA09_SCL_MISO, U1.O
  N4: Part1.D1_A0_PA02, Part2.DATAIN
  N5: Part1.D0_A4_PA08_SDA, PIR1.SIG
  VDD: Part1.VBUS, PIR1.VDD, PIR2.VDD, Part2.+5V, R1.P$2

notes:
  Top of stairs sensor
  Bottom of stairs sensor

custom parts:
  NeoPixel Stick: Make your own little LED strip arrangement with this stick of NeoPixel LEDs. We crammed 8 of the tiny 5050 (5mm x 5mm) smart RGB LEDs onto a PCB with mounting holes and a chainable design. Use only one microcontroller pin to control as many as you can chain together! Each LED is addressable as the driver chip is inside the LED. Each one has ~18mA constant current drive so the color will be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
