# Fritzing sketch Stairways as built (saved by Fritzing 0.9.3b)
perfboards: 1

parts:
  Part1 = Adafruit Trinket M0 [part_number="Adafruit #3500"]
  PIR1 = PIR sensor  # not connected
  PIR2 = PIR sensor
  J1 = Power Jack [package=power_jack_pth_lock]
  S1 = Toggle Switch [package=THT]
  R1 = Photocell (LDR) [package=THT]
  R2 = Resistor [tolerance=±5% resistance=3.3k package=THT]
  JP2 = Header 4 [package=jst-4-pth]  # not connected
  JP3 = Header 4 [package=jst-4-pth]
  JP4 = Header 4 [package=jst-4-pth]  # not connected
  JP5 = Header 4 [package=jst-4-pth]  # not connected
  Part3 = Adafruit JST breakout [part_number="Adafruit #1862"]  # not connected
  Part4 = Adafruit JST breakout [part_number="Adafruit #1862"]
  Part5 = Adafruit JST breakout [part_number="Adafruit #1862"]
  Part6 = Adafruit JST breakout [part_number="Adafruit #1862"]
  Part7 = Adafruit JST breakout [part_number="Adafruit #1862"]
  Part8 = Adafruit JST breakout [part_number="Adafruit #1862"]
  Part2 = NeoPixel Stick [part_number=1426]
  JP6 = Header 3 [package=jst-3-pth]
  JP7 = Header 3 [package=jst-3-pth]
  Part9 = Adafruit JST breakout [part_number="Adafruit #1862"]  # not connected
  C1 = Capacitor Polarized [package=cpol-radial-100uf-25v]

nets:
  N1: Part1.GND, Part8.V-
  N2: Part1.D4_A2_PA06_TXD_MOSI, Part7.V-
  N3: Part1.D3_A3_PA07_RXD_SCK, Part1.!RESET, Part7.V+
  N4: Part1.D2_A1_PA09_SCL_MISO, Part8.V+
  N5: Part1.D1_A0_PA02, Part6.V+
  N6: Part1.D0_A4_PA08_SDA, Part6.V-
  N7: PIR2.VDD, R1.pin_0
  N8: J1.GND, JP7.2
  N9: J1.PWR, JP7.3, C1.+
  N10: S1.L1, Part4.V+
  N11: S1.COM, Part4.V-
  N12: R2.Pin_1, JP3.4, Part5.V+
  N13: Part2.+5V, JP6.3
  N14: Part2.DATAIN, JP6.1
  N15: Part2.GND, JP6.2

notes:
  lower stairway sensor
  upper stairway sensor
  Trinket pin assignments
  D0: Upper PIR
  D1: Neopixel strip
  D2: Mode switch (pull-up)
  D3: Photoresistor (analog in)
  D4: Lower PIR
  JST connectors (internal):
  1r: D1 - neopixel
  1b: D0 - Upper PIR
  2r: D2 - mode switch
  2b: GND - mode switch
  •r: D3 - Lower PIR
  •b: D4 - Photoresistor
  JST4-1 (external)
  red - upper PIR +5
  grn - upper PIR sensor
  blk - upper PIR GND
  blu - n/c
  jst1
  jst3
  jst2
  jst4-1
  jst4-2
  JST4-2 (external)
  red - lower PIR +5
  grn - lower PIR sensor
  blk - lower PIR GND
  blu - photoresistor
  JST3-1 (external)
  red - neopixels +5
  grn - neopixel clock and data
  blk - neopixels GND
  jst3-1

custom parts:
  Adafruit JST breakout: A simple 2-pin connector soldered onto a breadboard-friendly breakout. This is compatible with the "JST PH 2-pin" connector. Mates perfectly with all our 1-cell LiPoly and LiIon batteries as well as our 6V coin cell holder and 3xAAA battery pack. We also have simple JST pigtails that mate with this connector.
  NeoPixel Stick: Make your own little LED strip arrangement with this stick of NeoPixel LEDs. We crammed 8 of the tiny 5050 (5mm x 5mm) smart RGB LEDs onto a PCB with mounting holes and a chainable design. Use only one microcontroller pin to control as many as you can chain together! Each LED is addressable as the driver chip is inside the LED. Each one has ~18mA constant current drive so the color will be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
